# Fritzing sketch Home Automation System (saved by Fritzing 0.9.3b)
breadboards: 1

parts:
  Part1 = Arduino Uno (Rev3)
  Part2 = RFID USB Reader
  RHT1 = Humidity and Temperature Sensor RHT03
  J1 = Basic Servo
  LED1 = LED - 5mm [color="Red (633nm)" package="5 mm [THT]"]
  LED2 = LED - 5mm [color="Red (633nm)" package="5 mm [THT]"]
  R1 = Resistor [tolerance=±5% resistance=220 package=THT]
  R2 = Resistor [tolerance=±5% resistance=220 package=THT]
  R3 = Resistor [tolerance=±5% resistance=220 package=THT]
  R4 = Resistor [tolerance=±5% resistance=220 package=THT]
  R5 = Resistor [tolerance=±5% resistance=220 package=THT]
  LED3 = LED - 5mm [color="Red (633nm)" package="5 mm [THT]"]
  LED4 = LED - 5mm [color="Red (633nm)" package="5 mm [THT]"]
  LED5 = LED - 5mm [color="Red (633nm)" package="5 mm [THT]"]

nets:
  N1: Part1.D8, RHT1.Data-signal
  N2: Part1.D9_PWM, Part2.CP
  N3: Part1.D10_PWM/SS, Part2.VCC
  N4: Part1.D11_PWM/MOSI, Part2.TX-O
  N5: Part1.D12/MISO, Part2.TX-O-RS232
  N6: Part1.D13/SCK, Part2.GND
  GND: Part1.GND, Part2.ANT2, RHT1.GND_1, J1.gnd, R1.Pin_1, R2.Pin_1, R3.Pin_1, R4.Pin_1, R5.Pin_1
  N7: Part1.D2, LED4.anode
  N8: Part1.D3_PWM, J1.pulse
  N9: Part1.D4, LED3.anode
  N10: Part1.D5_PWM, LED5.anode
  N11: Part1.D6_PWM, LED1.anode
  N12: Part1.D7, LED2.anode
  N13: Part1.3V3, Part2.GNDT
  VCC: Part1.5V, RHT1.Vcc, J1.vcc
  N14: LED1.cathode, R2.Pin_0
  N15: LED2.cathode, R1.Pin_0
  N16: R3.Pin_0, LED3.cathode
  N17: R4.Pin_0, LED4.cathode
  N18: R5.Pin_0, LED5.cathode
